// Logisim project clock.circ as structural Verilog: 7 circuits, main circuit organism_clock
module organism_clock (
  output [3:0] out_1,
  output [3:0] out_2,
  output [3:0] out_3,
  output [3:0] out_4,
  output [3:0] out_5,
  output [3:0] out_6
);

  wire atom_0_5_1_overflow, atom_0_5_2_overflow, atom_0_9_hour_1_overflow, atom_0_9_minute_1_overflow,
       atom_0_9_second_1_overflow, clock_1_out;
  wire [3:0] atom_0_2_1_out, atom_0_5_1_out, atom_0_5_2_out, atom_0_9_hour_1_out, atom_0_9_minute_1_out,
       atom_0_9_second_1_out;

  Clock clock_1 (.out(clock_1_out));
  atom_0_2 atom_0_2_1 (.in(out_1), .out(atom_0_2_1_out), .in_overflow(atom_0_9_hour_1_overflow));  // open: overflow
  atom_0_9_hour atom_0_9_hour_1 (
    ._2nd(out_1), .in(out_2), .overflow(atom_0_9_hour_1_overflow), .out(atom_0_9_hour_1_out),
    .in_overflow(atom_0_5_1_overflow));
  molecule_flipflop_d molecule_flipflop_d_1 (.d(atom_0_2_1_out), .q(out_1), .clk(clock_1_out));
  Hex_Digit_Display hex_digit_display_1 (.value(out_1));  // open: dp
  molecule_flipflop_d molecule_flipflop_d_2 (.d(atom_0_9_hour_1_out), .q(out_2), .clk(clock_1_out));
  Hex_Digit_Display hex_digit_display_2 (.value(out_2));  // open: dp
  atom_0_5 atom_0_5_1 (
    .in(out_3), .overflow(atom_0_5_1_overflow), .out(atom_0_5_1_out), .in_overflow(atom_0_9_minute_1_overflow));
  molecule_flipflop_d molecule_flipflop_d_3 (.d(atom_0_5_1_out), .q(out_3), .clk(clock_1_out));
  Hex_Digit_Display hex_digit_display_3 (.value(out_3));  // open: dp
  atom_0_9_minute atom_0_9_minute_1 (
    .in(out_4), .overflow(atom_0_9_minute_1_overflow), .out(atom_0_9_minute_1_out),
    .in_overflow(atom_0_5_2_overflow));
  molecule_flipflop_d molecule_flipflop_d_4 (.d(atom_0_9_minute_1_out), .q(out_4), .clk(clock_1_out));
  Hex_Digit_Display hex_digit_display_4 (.value(out_5));  // open: dp
  Hex_Digit_Display hex_digit_display_5 (.value(out_4));  // open: dp
  atom_0_5 atom_0_5_2 (
    .in(out_5), .overflow(atom_0_5_2_overflow), .out(atom_0_5_2_out), .in_overflow(atom_0_9_second_1_overflow));
  Hex_Digit_Display hex_digit_display_6 (.value(out_6));  // open: dp
  atom_0_9_second atom_0_9_second_1 (.in(out_6), .overflow(atom_0_9_second_1_overflow), .out(atom_0_9_second_1_out));
  molecule_flipflop_d molecule_flipflop_d_5 (.d(atom_0_5_2_out), .q(out_5), .clk(clock_1_out));
  molecule_flipflop_d molecule_flipflop_d_6 (.d(atom_0_9_second_1_out), .q(out_6), .clk(clock_1_out));

  // Notes on the sheet:
  //   :
  //   :
endmodule

module molecule_flipflop_d (
  input  [3:0] d,
  input  clk,
  output [3:0] q
);

  D_Flip_Flop d_ff_1 (.clk(clk), .D(d[0]), .Q(q[0]));  // open: Qn, preset, en, reset
  D_Flip_Flop d_ff_2 (.clk(clk), .D(d[1]), .Q(q[1]));  // open: Qn, preset, en, reset
  D_Flip_Flop d_ff_3 (.clk(clk), .D(d[2]), .Q(q[2]));  // open: Qn, preset, en, reset
  D_Flip_Flop d_ff_4 (.clk(clk), .D(d[3]), .Q(q[3]));  // open: Qn, preset, en, reset
endmodule

module atom_0_9_second (
  input  [3:0] in,
  output overflow,
  output [3:0] out
);

  wire [3:0] adder_1_out;

  Adder #(.width(4)) adder_1 (.a(in), .b(4'b0001), .out(adder_1_out));  // open: cin, cout
  and and_1 (overflow, in[0], ~in[1], ~in[2], in[3]);  // AND_Gate
  Multiplexer #(.width(4), .enable("false")) multiplexer_1 (
    .in0(adder_1_out), .in1(4'b0000), .out(out), .sel(overflow));
endmodule

module atom_0_9_minute (
  input  in_overflow,
  input  [3:0] in,
  output overflow,
  output [3:0] out
);

  wire and_1_out, and_2_out;
  wire [3:0] adder_1_out, multiplexer_1_out;

  Adder #(.width(4)) adder_1 (.a(in), .b(4'b0001), .out(adder_1_out));  // open: cin, cout
  Multiplexer #(.width(4), .enable("false")) multiplexer_1 (
    .in0(in), .in1(adder_1_out), .out(multiplexer_1_out), .sel(in_overflow));
  and and_1 (and_1_out, in[0], ~in[1], ~in[2], in[3]);  // AND_Gate
  and and_2 (and_2_out, in_overflow, and_1_out);
  Multiplexer #(.width(4), .enable("false")) multiplexer_2 (
    .in0(multiplexer_1_out), .in1(4'b0000), .out(out), .sel(and_2_out));
  and and_3 (overflow, and_1_out, in_overflow);
endmodule

module atom_0_9_hour (
  input  [3:0] _2nd,
  input  in_overflow,
  input  [3:0] in,
  output overflow,
  output [3:0] out
);

  wire and_1_out, and_2_out, and_3_out, and_5_out, multiplexer_2_out;
  wire [3:0] adder_1_out, multiplexer_1_out;

  Multiplexer #(.width(4), .enable("false")) multiplexer_1 (
    .in0(in), .in1(adder_1_out), .out(multiplexer_1_out), .sel(in_overflow));
  Adder #(.width(4)) adder_1 (.a(in), .b(4'b0001), .out(adder_1_out));  // open: cin, cout
  and and_1 (and_1_out, ~_2nd[0], _2nd[1], ~_2nd[2], ~_2nd[3]);  // AND_Gate
  and and_2 (and_2_out, in[0], ~in[1], ~in[2], in[3]);  // AND_Gate
  and and_3 (and_3_out, in[0], in[1], ~in[2], ~in[3]);  // AND_Gate
  Multiplexer #(.enable("false")) multiplexer_2 (
    .in0(and_2_out), .in1(and_3_out), .out(multiplexer_2_out), .sel(and_1_out));
  and and_4 (overflow, multiplexer_2_out, in_overflow);
  and and_5 (and_5_out, in_overflow, multiplexer_2_out);
  Multiplexer #(.width(4), .enable("false")) multiplexer_3 (
    .in0(multiplexer_1_out), .in1(4'b0000), .out(out), .sel(and_5_out));
endmodule

module atom_0_5 (
  input  in_overflow,
  input  [3:0] in,
  output overflow,
  output [3:0] out
);

  wire and_1_out, and_2_out;
  wire [3:0] adder_1_out, multiplexer_1_out;

  Adder #(.width(4)) adder_1 (.a(in), .b(4'b0001), .out(adder_1_out));  // open: cin, cout
  Multiplexer #(.width(4), .enable("false")) multiplexer_1 (
    .in0(in), .in1(adder_1_out), .out(multiplexer_1_out), .sel(in_overflow));
  and and_1 (and_1_out, in[0], ~in[1], in[2], ~in[3]);  // AND_Gate
  and and_2 (and_2_out, in_overflow, and_1_out);
  Multiplexer #(.width(4), .enable("false")) multiplexer_2 (
    .in0(multiplexer_1_out), .in1(4'b0000), .out(out), .sel(and_2_out));
  and and_3 (overflow, and_1_out, in_overflow);
endmodule

module atom_0_2 (
  input  in_overflow,
  input  [3:0] in,
  output overflow,
  output [3:0] out
);

  wire and_1_out, and_2_out;
  wire [3:0] adder_1_out, multiplexer_1_out;

  Adder #(.width(4)) adder_1 (.a(in), .b(4'b0001), .out(adder_1_out));  // open: cin, cout
  Multiplexer #(.width(4), .enable("false")) multiplexer_1 (
    .in0(in), .in1(adder_1_out), .out(multiplexer_1_out), .sel(in_overflow));
  and and_1 (and_1_out, ~in[0], in[1], ~in[2], ~in[3]);  // AND_Gate
  and and_2 (and_2_out, in_overflow, and_1_out);
  Multiplexer #(.width(4), .enable("false")) multiplexer_2 (
    .in0(multiplexer_1_out), .in1(4'b0000), .out(out), .sel(and_2_out));
  and and_3 (overflow, and_1_out, in_overflow);
endmodule
