// Logisim project ula.circ as structural Verilog: 7 circuits, main circuit organism
module organism (
  input  [31:0] a,
  input  [31:0] b,
  input  [4:0] Sel,
  output [31:0] S
);

  wire molecule_32bits_1_overflow, molecule_32bits_1_zero;

  molecule_32bits molecule_32bits_1 (
    .Sel(Sel), .a(a), .overflow(molecule_32bits_1_overflow), .b(b), .S(S), .zero(molecule_32bits_1_zero));
  LED overflow (.in(molecule_32bits_1_overflow));
  LED zero (.in(molecule_32bits_1_zero));
endmodule

module molecule_32bits (
  input  [4:0] Sel,
  input  [31:0] a,
  input  [31:0] b,
  output overflow,
  output [31:0] S,
  output zero
);

  wire atom_main_1_out, atom_main_1_send, atom_main_2_out, atom_main_2_send, atom_main_3_out,
       atom_main_3_send, atom_main_4_out, atom_main_4_send, atom_main_5_out, atom_main_5_send,
       atom_main_6_out, atom_main_6_send, atom_main_7_out, atom_main_7_send, atom_main_8_out,
       atom_main_8_send, atom_main_9_out, atom_main_9_send, atom_main_10_out, atom_main_10_send,
       atom_main_11_out, atom_main_11_send, atom_main_12_out, atom_main_12_send, atom_main_13_out,
       atom_main_13_send, atom_main_14_out, atom_main_14_send, atom_main_15_out, atom_main_15_send,
       atom_main_16_out, atom_main_16_send, atom_main_17_out, atom_main_17_send, atom_main_18_out,
       atom_main_18_send, atom_main_19_out, atom_main_19_send, atom_main_20_out, atom_main_20_send,
       atom_main_21_out, atom_main_21_send, atom_main_22_out, atom_main_22_send, atom_main_23_out,
       atom_main_23_send, atom_main_24_out, atom_main_24_send, atom_main_25_out, atom_main_25_send,
       atom_main_26_out, atom_main_26_send, atom_main_27_out, atom_main_27_send, atom_main_28_out,
       atom_main_28_send, atom_main_29_out, atom_main_29_send, atom_main_30_out, atom_main_30_send,
       atom_main_31_out, atom_main_31_send, atom_main_32_out, atom_overflow_1_overflow, atom_signal_1_e;

  atom_zero atom_zero_1 (.a(S), .zero(zero));
  Multiplexer #(.select(5)) multiplexer_1 (
    .in0(atom_main_1_out), .in1(atom_main_1_out), .in2(atom_main_1_out), .in3(atom_main_1_out),
    .in4(atom_overflow_1_overflow), .in5(atom_main_1_out), .in6(atom_main_1_out), .in7(atom_main_1_out),
    .in8(atom_main_1_out), .in9(atom_main_1_out), .in10(atom_main_1_out), .in11(atom_main_1_out),
    .in12(atom_main_1_out), .in13(atom_main_1_out), .in14(atom_main_1_out), .in15(atom_main_1_out),
    .in16(atom_main_1_out), .in17(atom_main_1_out), .in18(atom_main_1_out), .in19(atom_main_1_out),
    .in20(atom_main_1_out), .in21(atom_main_1_out), .in22(atom_main_1_out), .in23(atom_main_1_out),
    .in24(atom_main_1_out), .in25(atom_main_1_out), .in26(atom_main_1_out), .in27(atom_main_1_out),
    .in28(atom_main_1_out), .in29(atom_main_1_out), .in30(atom_main_1_out), .in31(atom_main_1_out),
    .out(overflow), .sel(Sel));  // open: en
  atom_signal atom_signal_1 (.Sel(Sel), .a(a[31]), .E(atom_signal_1_e));
  atom_overflow atom_overflow_1 (.overflow(atom_overflow_1_overflow), .a(a[31]), .b(b[31]), .S(S[31]));
  atom_main atom_main_1 (
    .a(a[31]), .b(b[31]), .in(atom_main_2_out), .S(S[31]), .out(atom_main_1_out), .Sel(Sel),
    .receive(atom_signal_1_e), .send(atom_main_1_send));
  atom_main atom_main_2 (
    .a(a[30]), .b(b[30]), .in(atom_main_3_out), .S(S[30]), .out(atom_main_2_out), .Sel(Sel),
    .receive(atom_main_1_send), .send(atom_main_2_send));
  atom_main atom_main_3 (
    .a(a[29]), .b(b[29]), .in(atom_main_4_out), .S(S[29]), .out(atom_main_3_out), .Sel(Sel),
    .receive(atom_main_2_send), .send(atom_main_3_send));
  atom_main atom_main_4 (
    .a(a[28]), .b(b[28]), .in(atom_main_5_out), .S(S[28]), .out(atom_main_4_out), .Sel(Sel),
    .receive(atom_main_3_send), .send(atom_main_4_send));
  atom_main atom_main_5 (
    .a(a[27]), .b(b[27]), .in(atom_main_6_out), .S(S[27]), .out(atom_main_5_out), .Sel(Sel),
    .receive(atom_main_4_send), .send(atom_main_5_send));
  atom_main atom_main_6 (
    .a(a[26]), .b(b[26]), .in(atom_main_7_out), .S(S[26]), .out(atom_main_6_out), .Sel(Sel),
    .receive(atom_main_5_send), .send(atom_main_6_send));
  atom_main atom_main_7 (
    .a(a[25]), .b(b[25]), .in(atom_main_8_out), .S(S[25]), .out(atom_main_7_out), .Sel(Sel),
    .receive(atom_main_6_send), .send(atom_main_7_send));
  atom_main atom_main_8 (
    .a(a[24]), .b(b[24]), .in(atom_main_9_out), .S(S[24]), .out(atom_main_8_out), .Sel(Sel),
    .receive(atom_main_7_send), .send(atom_main_8_send));
  atom_main atom_main_9 (
    .a(a[23]), .b(b[23]), .in(atom_main_11_out), .S(S[23]), .out(atom_main_9_out), .Sel(Sel),
    .receive(atom_main_8_send), .send(atom_main_9_send));
  atom_main atom_main_10 (
    .a(a[21]), .b(b[21]), .in(atom_main_12_out), .S(S[21]), .out(atom_main_10_out), .Sel(Sel),
    .receive(atom_main_11_send), .send(atom_main_10_send));
  atom_main atom_main_11 (
    .a(a[22]), .b(b[22]), .in(atom_main_10_out), .S(S[22]), .out(atom_main_11_out), .Sel(Sel),
    .receive(atom_main_9_send), .send(atom_main_11_send));
  atom_main atom_main_12 (
    .a(a[20]), .b(b[20]), .in(atom_main_13_out), .S(S[20]), .out(atom_main_12_out), .Sel(Sel),
    .receive(atom_main_10_send), .send(atom_main_12_send));
  atom_main atom_main_13 (
    .a(a[19]), .b(b[19]), .in(atom_main_14_out), .S(S[19]), .out(atom_main_13_out), .Sel(Sel),
    .receive(atom_main_12_send), .send(atom_main_13_send));
  atom_main atom_main_14 (
    .a(a[18]), .b(b[18]), .in(atom_main_15_out), .S(S[18]), .out(atom_main_14_out), .Sel(Sel),
    .receive(atom_main_13_send), .send(atom_main_14_send));
  atom_main atom_main_15 (
    .a(a[17]), .b(b[17]), .in(atom_main_16_out), .S(S[17]), .out(atom_main_15_out), .Sel(Sel),
    .receive(atom_main_14_send), .send(atom_main_15_send));
  atom_main atom_main_16 (
    .a(a[16]), .b(b[16]), .in(atom_main_17_out), .S(S[16]), .out(atom_main_16_out), .Sel(Sel),
    .receive(atom_main_15_send), .send(atom_main_16_send));
  atom_main atom_main_17 (
    .a(a[15]), .b(b[15]), .in(atom_main_18_out), .S(S[15]), .out(atom_main_17_out), .Sel(Sel),
    .receive(atom_main_16_send), .send(atom_main_17_send));
  atom_main atom_main_18 (
    .a(a[14]), .b(b[14]), .in(atom_main_19_out), .S(S[14]), .out(atom_main_18_out), .Sel(Sel),
    .receive(atom_main_17_send), .send(atom_main_18_send));
  atom_main atom_main_19 (
    .a(a[13]), .b(b[13]), .in(atom_main_20_out), .S(S[13]), .out(atom_main_19_out), .Sel(Sel),
    .receive(atom_main_18_send), .send(atom_main_19_send));
  atom_main atom_main_20 (
    .a(a[12]), .b(b[12]), .in(atom_main_21_out), .S(S[12]), .out(atom_main_20_out), .Sel(Sel),
    .receive(atom_main_19_send), .send(atom_main_20_send));
  atom_main atom_main_21 (
    .a(a[11]), .b(b[11]), .in(atom_main_22_out), .S(S[11]), .out(atom_main_21_out), .Sel(Sel),
    .receive(atom_main_20_send), .send(atom_main_21_send));
  atom_main atom_main_22 (
    .a(a[10]), .b(b[10]), .in(atom_main_23_out), .S(S[10]), .out(atom_main_22_out), .Sel(Sel),
    .receive(atom_main_21_send), .send(atom_main_22_send));
  atom_main atom_main_23 (
    .a(a[9]), .b(b[9]), .in(atom_main_24_out), .S(S[9]), .out(atom_main_23_out), .Sel(Sel),
    .receive(atom_main_22_send), .send(atom_main_23_send));
  atom_main atom_main_24 (
    .a(a[8]), .b(b[8]), .in(atom_main_25_out), .S(S[8]), .out(atom_main_24_out), .Sel(Sel),
    .receive(atom_main_23_send), .send(atom_main_24_send));
  atom_main atom_main_25 (
    .a(a[7]), .b(b[7]), .in(atom_main_27_out), .S(S[7]), .out(atom_main_25_out), .Sel(Sel),
    .receive(atom_main_24_send), .send(atom_main_25_send));
  atom_main atom_main_26 (
    .a(a[5]), .b(b[5]), .in(atom_main_28_out), .S(S[5]), .out(atom_main_26_out), .Sel(Sel),
    .receive(atom_main_27_send), .send(atom_main_26_send));
  atom_main atom_main_27 (
    .a(a[6]), .b(b[6]), .in(atom_main_26_out), .S(S[6]), .out(atom_main_27_out), .Sel(Sel),
    .receive(atom_main_25_send), .send(atom_main_27_send));
  atom_main atom_main_28 (
    .a(a[4]), .b(b[4]), .in(atom_main_29_out), .S(S[4]), .out(atom_main_28_out), .Sel(Sel),
    .receive(atom_main_26_send), .send(atom_main_28_send));
  atom_main atom_main_29 (
    .a(a[3]), .b(b[3]), .in(atom_main_30_out), .S(S[3]), .out(atom_main_29_out), .Sel(Sel),
    .receive(atom_main_28_send), .send(atom_main_29_send));
  atom_main atom_main_30 (
    .a(a[2]), .b(b[2]), .in(atom_main_31_out), .S(S[2]), .out(atom_main_30_out), .Sel(Sel),
    .receive(atom_main_29_send), .send(atom_main_30_send));
  atom_main atom_main_31 (
    .a(a[1]), .b(b[1]), .in(atom_main_32_out), .S(S[1]), .out(atom_main_31_out), .Sel(Sel),
    .receive(atom_main_30_send), .send(atom_main_31_send));
  atom_main atom_main_32 (
    .a(a[0]), .b(b[0]), .in(1'b0), .S(S[0]), .out(atom_main_32_out), .Sel(Sel), .receive(atom_main_31_send));  // open: send
endmodule

module molecule_2bits (
  input  [4:0] in_1,
  input  [1:0] in_2,
  input  [1:0] in_3,
  input  in_4,
  output [1:0] out_5,
  output out_6
);

  wire atom_main_1_send, atom_main_2_out, atom_main_2_send, atom_signal_1_e;

  atom_signal atom_signal_1 (.Sel(in_1), .a(in_2[1]), .E(atom_signal_1_e));
  atom_main atom_main_1 (
    .a(in_2[1]), .b(in_3[1]), .in(atom_main_2_out), .S(out_5[1]), .out(out_6), .Sel(in_1),
    .receive(atom_signal_1_e), .send(atom_main_1_send));
  atom_main atom_main_2 (
    .a(in_2[0]), .b(in_3[0]), .in(in_4), .S(out_5[0]), .out(atom_main_2_out), .Sel(in_1),
    .receive(atom_main_1_send), .send(atom_main_2_send));
  LED led_1 (.in(atom_main_2_send));
endmodule

module atom_main (
  input  [4:0] Sel,
  input  a,
  input  b,
  input  receive,
  input  in,
  output S,
  output send,
  output out
);

  wire adder_1_cout, adder_1_out, and_1_out, and_2_out, and_3_out, nand_1_out, or_1_out, subtractor_1_bout,
       subtractor_1_out, xor_1_out;

  and and_1 (and_1_out, a, b);
  or or_1 (or_1_out, a, b);
  Adder #(.width(1)) adder_1 (.a(a), .b(b), .out(adder_1_out), .cin(in), .cout(adder_1_cout));
  Subtractor #(.width(1)) subtractor_1 (.a(a), .b(b), .out(subtractor_1_out), .bin(in), .bout(subtractor_1_bout));
  nand nand_1 (nand_1_out, a, b);
  xor xor_1 (xor_1_out, a, b);
  Multiplexer #(.select(5)) multiplexer_1 (
    .in0(and_1_out), .in1(or_1_out), .in2(nand_1_out), .in3(xor_1_out), .in4(adder_1_out), .in5(adder_1_out),
    .in6(subtractor_1_out), .in7(in), .in8(receive), .in9(receive), .out(S), .sel(Sel));  // open: in10, in11, in12, in13, in14, in15, in16, in17, in18, in19, in20, in21, in22, in23, in24, in25, in26, in27, in28, in29, in30, in31, en
  Multiplexer #(.select(5)) multiplexer_2 (
    .in0(1'b0), .in1(1'b0), .in2(1'b0), .in3(1'b0), .in4(adder_1_cout), .in5(adder_1_cout),
    .in6(subtractor_1_bout), .in7(a), .in8(1'b0), .in9(1'b0), .in10(1'b0), .in11(1'b0), .in12(1'b0),
    .in13(1'b0), .in14(1'b0), .in15(1'b0), .in16(1'b0), .in17(1'b0), .in18(1'b0), .in19(1'b0), .in20(1'b0),
    .in21(1'b0), .in22(1'b0), .in23(1'b0), .in24(1'b0), .in25(1'b0), .in26(1'b0), .in27(1'b0), .in28(1'b0),
    .in29(1'b0), .in30(1'b0), .in31(1'b0), .out(out), .sel(Sel));  // open: en
  and and_2 (and_2_out, ~Sel[0], ~Sel[1], ~Sel[2], Sel[3], ~Sel[4], a);  // AND_Gate
  and and_3 (and_3_out, Sel[0], ~Sel[1], ~Sel[2], Sel[3], ~Sel[4], a);  // AND_Gate
  xor xor_2 (send, and_2_out, and_3_out);
endmodule

module atom_overflow (
  input  a,
  input  b,
  input  S,
  output overflow
);

  wire and_1_out, and_2_out, not_1_out, not_2_out, not_3_out;

  or or_1 (overflow, and_1_out, and_2_out);
  and and_1 (and_1_out, not_1_out, not_2_out, S);
  and and_2 (and_2_out, a, b, not_3_out);
  not not_1 (not_1_out, a);
  not not_2 (not_2_out, b);
  not not_3 (not_3_out, S);
endmodule

module atom_zero (
  input  [31:0] a,
  output zero
);

  and and_1 (zero, ~a[31], ~a[30], ~a[29], ~a[28], ~a[27], ~a[26], ~a[25], ~a[24], ~a[23], ~a[22], ~a[21], ~a[20], ~a[19], ~a[18], ~a[17], ~a[16], ~a[15], ~a[14], ~a[13], ~a[12], ~a[11], ~a[10], ~a[9], ~a[8], ~a[7], ~a[6], ~a[5], ~a[4], ~a[3], ~a[2], ~a[1], ~a[0]);  // AND_Gate
endmodule

module atom_signal (
  input  [4:0] Sel,
  input  a,
  output E
);

  and and_1 (E, ~Sel[4], Sel[3], ~Sel[2], ~Sel[1], Sel[0], a);  // AND_Gate
endmodule
